# Fritzing sketch FritzingSketch (saved by Fritzing 0.9.3b)
breadboards: 2

parts:
  Part1 = Arduino Uno (Rev3)
  J1 = Piezo Speaker
  DFRobot_DFPlayer_Mini1 = DFRobot DFPlayer Mini [part_number=DFR0299]
  SP1 = SPEAKER [package=pcb_mount_speaker]
  R1 = Resistor [tolerance=±5% resistance=1k package=THT]
  U1 = 7-SEGMENT-DISPLAY [package=7-segment-display]
  U2 = 7-SEGMENT-DISPLAY [package=7-segment-display]
  U3 = 74HC595 [package="DIP16 [THT]"]
  U4 = 74HC595 [package="DIP16 [THT]"]

nets:
  N1: Part1.A0, U3.DS, U4.Q7', U4.DS
  N2: Part1.A1, U3.ST_CP, U4.ST_CP
  N3: Part1.A2, U3.SH_CP, U4.SH_CP
  N4: Part1.D11_PWM/MOSI, J1.pin2
  N5: Part1.D12/MISO, R1.Pin_1
  N6: Part1.D13/SCK, DFRobot_DFPlayer_Mini1.DAC_R
  GND: Part1.GND, J1.pin1, DFRobot_DFPlayer_Mini1.GND-1, DFRobot_DFPlayer_Mini1.GND-2, U3.GND, U3.OE, U4.GND, U4.OE
  VCC: Part1.5V, DFRobot_DFPlayer_Mini1.VCC, U1.F, U2.F, U3.MR, U3.VCC, U4.MR, U4.VCC
  N7: DFRobot_DFPlayer_Mini1.RX, R1.Pin_0
  N8: DFRobot_DFPlayer_Mini1.SPK_1, SP1.-
  N9: DFRobot_DFPlayer_Mini1.SPK_2, SP1.+
  N10: U1.E, U3.Q5
  N11: U1.D, U3.Q2
  N12: U1.G1, U3.Q3
  N13: U1.DP, U3.Q4
  N14: U1.A, U3.Q1
  N15: U1.G2, U3.Q0
  N16: U1.G, U3.Q6
  N17: U2.E, U4.Q5
  N18: U2.D, U4.Q4
  N19: U2.G1, U4.Q3
  N20: U2.DP, U4.Q2
  N21: U2.A, U4.Q1
  N22: U2.G2, U4.Q0
  N23: U2.G, U4.Q6
